// Logisim project SAP3.circ as structural Verilog: 14 circuits, main circuit main
module main (
  input  in_1,
  input  in_2
);

  wire AccEn, AccIn, ALU0, ALU1, ALU2, ALU3, alu_1_cfout, alu_1_fen, ALUOut, and_1_out, and_2_out, and_3_out,
       CF, CLK, clock_1_out, DisEn, DOWNLoad, HLT, IE, JM, JMP, JNZ, JZ, MAREN, MARSel, MDREn, not_1_out,
       or_1_out, or_2_out, or_3_out, RAMOut, RAMWE, s_r_ff_1_q, SF, TempEn, TempIn, undriven, undriven_3,
       undriven_4, undriven_5, undriven_6, undriven_7, UPLoad, ZF;
  wire [3:0] counter_1_q, display_1_p2, display_1_p2_2, display_1_p3, display_1_p3_2, display_1_p5,
       display_1_p5_2;
  wire [7:0] Accumulator_currentdata, B_currentdata, C_currentdata, controlled_buffer_1_out, D_currentdata,
       display_1_p6, display_1_p8, E_currentdata, H_currentdata, L_currentdata, ram_1_dout,
       ramcontroller_1_ramwr, register_1_q, Stack1_dataout, Temp_currentdata, undriven_2;
  wire [15:0] ramcontroller_1_addr;
  wire [31:8] MicroCode_data;

  or or_1 (or_1_out, HLT, in_1);
  and and_1 (and_1_out, JM, SF);
  and and_2 (and_2_out, JNZ, ~ZF);  // AND_Gate
  S_R_Flip_Flop s_r_ff_1 (.S(HLT), .clk(or_1_out), .R(in_1), .Q(s_r_ff_1_q));  // open: Qn, preset, reset
  Clock clock_1 (.out(clock_1_out));
  or or_2 (or_2_out, and_1_out, or_3_out, JMP);
  or or_3 (or_3_out, and_2_out, and_3_out);
  and and_3 (and_3_out, ZF, JZ);
  and and_4 (CLK, ~s_r_ff_1_q, clock_1_out, in_2);  // AND_Gate
  RAMController ramcontroller_1 (
    .UpperLoad(UPLoad), .LowerLoad(DOWNLoad), .MARSel(MARSel),
    .MAR({Stack1_dataout, controlled_buffer_1_out}), .MAREn(MAREN), .Clk(CLK), .Reset(in_1), .MDREn(MDREn),
    .Addr(ramcontroller_1_addr), .RAMWr(ramcontroller_1_ramwr));
  Counter #(.max('ha), .width(4)) counter_1 (
    .Q(counter_1_q), .clk(not_1_out), .clr(undriven));  // open: load, D, count, carry, up
  // NOT_Gate not_1 has open pins: in=open, out=not_1_out
  RAM #(.addrWidth(16)) ram_1 (
    .addr(ramcontroller_1_addr), .we(RAMWE), .oe(1'b1), .clk(CLK), .din(ramcontroller_1_ramwr),
    .dout(ram_1_dout));
  ROM #(.addrWidth(12), .dataWidth(32)) MicroCode (
    .addr({register_1_q, counter_1_q}),
    .data({MicroCode_data[31:29], DisEn, JM, JZ, JNZ, JMP, ALU3, ALU2, ALU1, ALU0, HLT, ALUOut, MicroCode_data[17:8], RAMWE, UPLoad, DOWNLoad, MARSel, IE, RAMOut, MAREN, MDREn}));
  Register register_1 (.D(undriven_2), .en(IE), .Q(register_1_q));  // open: clk, clr
  assign controlled_buffer_1_out = RAMOut ? ram_1_dout : 8'bz;  // Controlled_Buffer controlled_buffer_1
  _7_Segment_Display u_7_segment_display_1 (
    .g(display_1_p2_2[2]), .f(display_1_p2_2[1]), .a(display_1_p2[0]), .b(display_1_p2[1]),
    .e(display_1_p2_2[0]), .d(display_1_p2[3]), .c(display_1_p2[2]));  // open: dp
  // Probe on Accumulator_currentdata
  Regs Accumulator (
    .DataIn(controlled_buffer_1_out), .Load(AccIn), .Clk(CLK), .Clr(in_1), .RegEn(AccEn),
    .CurrentData(Accumulator_currentdata), .DataOut(controlled_buffer_1_out));
  ALU alu_1 (
    .A(Accumulator_currentdata), .B(Temp_currentdata), .CFIn(CF), .ALUSel({ALU3, ALU2, ALU1, ALU0}),
    .ALUOut(ALUOut), .CFOut(alu_1_cfout), .FEn(alu_1_fen), .Product(controlled_buffer_1_out));
  // Probe on Temp_currentdata
  Regs Temp (
    .DataIn(controlled_buffer_1_out), .Load(TempIn), .Clk(CLK), .Clr(in_1), .RegEn(TempEn),
    .CurrentData(Temp_currentdata), .DataOut(controlled_buffer_1_out));
  // Probe on B_currentdata
  Regs B (
    .DataIn(controlled_buffer_1_out), .Clk(undriven_5), .CurrentData(B_currentdata),
    .DataOut(controlled_buffer_1_out));  // open: Load, Clr, RegEn
  // Probe on D_currentdata
  Regs D (
    .DataIn(controlled_buffer_1_out), .Clk(undriven_5), .CurrentData(D_currentdata),
    .DataOut(controlled_buffer_1_out));  // open: Load, Clr, RegEn
  // Probe on H_currentdata
  Regs H (
    .DataIn(controlled_buffer_1_out), .Clk(undriven_5), .CurrentData(H_currentdata),
    .DataOut(controlled_buffer_1_out));  // open: Load, Clr, RegEn
  Regs Stack1 (
    .DataIn(Stack1_dataout), .Load(undriven_7), .Clk(undriven_4), .Clr(undriven_6), .RegEn(undriven_3),
    .DataOut(Stack1_dataout));  // open: CurrentData
  _7_Segment_Display u_7_segment_display_2 (
    .g(display_1_p3_2[2]), .f(display_1_p3_2[1]), .a(display_1_p3[0]), .b(display_1_p3[1]),
    .e(display_1_p3_2[0]), .d(display_1_p3[3]), .c(display_1_p3[2]));  // open: dp
  // Display display_1: pin names not known; wires that end beside it: DisEn, {display_1_p2_2, display_1_p2}, {display_1_p3_2, display_1_p3}, DOWNLoad, {display_1_p5_2, display_1_p5}, display_1_p6, UPLoad, display_1_p8
  _7_Segment_Display u_7_segment_display_3 (
    .g(display_1_p5_2[2]), .f(display_1_p5_2[1]), .a(display_1_p5[0]), .b(display_1_p5[1]),
    .e(display_1_p5_2[0]), .d(display_1_p5[3]), .c(display_1_p5[2]));  // open: dp
  PC pc_1 (
    .LOAD({Stack1_dataout, controlled_buffer_1_out}), .BusData({Stack1_dataout, controlled_buffer_1_out}));  // open: Jump, PCEn, Clk, PCOut, PCClr
  Regs Stack0 (
    .DataIn(controlled_buffer_1_out), .Load(undriven_7), .Clk(undriven_4), .Clr(undriven_6),
    .RegEn(undriven_3), .DataOut(controlled_buffer_1_out));  // open: CurrentData
  FlagReg flagreg_1 (
    .BusALU(controlled_buffer_1_out), .CarryF(alu_1_cfout), .Clk(CLK), .Clr(in_1), .FEn(alu_1_fen), .ZF(ZF),
    .SF(SF), .CF(CF));
  _7_Segment_Display u_7_segment_display_4 (
    .g(display_1_p6[6]), .f(display_1_p6[5]), .a(display_1_p6[0]), .b(display_1_p6[1]), .e(display_1_p6[4]),
    .d(display_1_p6[3]), .c(display_1_p6[2]));  // open: dp
  // Probe on C_currentdata
  Regs C (
    .DataIn(controlled_buffer_1_out), .Clk(undriven_5), .CurrentData(C_currentdata),
    .DataOut(controlled_buffer_1_out));  // open: Load, Clr, RegEn
  // Probe on E_currentdata
  Regs E (
    .DataIn(controlled_buffer_1_out), .Clk(undriven_5), .CurrentData(E_currentdata),
    .DataOut(controlled_buffer_1_out));  // open: Load, Clr, RegEn
  // Probe on L_currentdata
  Regs L (
    .DataIn(controlled_buffer_1_out), .Clk(undriven_5), .CurrentData(L_currentdata),
    .DataOut(controlled_buffer_1_out));  // open: Load, Clr, RegEn
  _7_Segment_Display u_7_segment_display_5 (
    .g(display_1_p8[6]), .f(display_1_p8[5]), .a(display_1_p8[0]), .b(display_1_p8[1]), .e(display_1_p8[4]),
    .d(display_1_p8[3]), .c(display_1_p8[2]));  // open: dp

  // Other names for the same wires on the sheet: ALUSel[3:0] = {ALU3, ALU2, ALU1, ALU0}; Clr = in_1; RUN = in_2

  // Notes on the sheet:
  //   HLT: 76
  //   INC A: 3C
  //   LDA: 3A
  //   DISP By: 10
  //   DISP A: 0F
  //   ADD C: 81
  //   ADD B: 80
  //   STA Addr: 32
  //   ADC B: 88
  //   MVI C: 0E
  //   MVI A, By: 3E
  //   MVI B, By: 06
  //   contents of MicroCode (hex, n*v repeats v):
  //   3 20c 94*0 3 20c 3 2204 124*0 3 20c 3 604 12*0 3 20c 4020 10000000 12*0 3 20c 3 244 3 224 10000000
  //   537*0 3 20c 3 244 3 224 4100 90 120*0 3 20c 3 244 3 224 10 8004 24*0 3 20c 248000 29*0 3 20c 3 8204
  //   892*0 3 20c 80000 157*0 3 20c 21000 48000 12*0 3 20c 20800 48000 108*0 3 20c 21000 448000
endmodule

module uCodeDecoder (
  input  [3:0] in_1,
  input  [3:0] in_2,
  input  [31:0] in_3,
  input  [3:0] in_4,
  input  [3:0] in_5,
  input  [3:0] in_6,
  input  [3:0] in_7,
  input  [3:0] in_8,
  input  [3:0] in_9,
  output [3:0] out_10,
  output [3:0] out_11,
  output [31:0] out_12,
  output [3:0] out_13,
  output [3:0] out_14,
  output [3:0] out_15,
  output [3:0] out_16,
  output [3:0] out_17,
  output [3:0] out_18
);


  assign out_10 = {in_3[0], in_3[1], in_3[2], in_3[3]};
  assign out_11 = {in_3[4], in_3[5], in_3[6], in_3[7]};
  assign out_12 = {in_9[0], in_9[1], in_9[2], in_9[3], in_8[0], in_8[1], in_8[2], in_8[3], in_7[0], in_7[1], in_7[2], in_7[3], in_6[0], in_6[1], in_6[2], in_6[3], in_5[0], in_5[1], in_5[2], in_5[3], in_4[0], in_4[1], in_4[2], in_4[3], in_2[0], in_2[1], in_2[2], in_2[3], in_1[0], in_1[1], in_1[2], in_1[3]};
  assign out_13 = {in_3[8], in_3[9], in_3[10], in_3[11]};
  assign out_14 = {in_3[12], in_3[13], in_3[14], in_3[15]};
  assign out_15 = {in_3[16], in_3[17], in_3[18], in_3[19]};
  assign out_16 = {in_3[20], in_3[21], in_3[22], in_3[23]};
  assign out_17 = {in_3[24], in_3[25], in_3[26], in_3[27]};
  assign out_18 = {in_3[28], in_3[29], in_3[30], in_3[31]};
endmodule

module PC (
  input  PCOut,
  input  [15:0] LOAD,
  input  PCClr,
  input  Jump,
  input  PCEn,
  input  Clk,
  output [15:0] BusData
);

  wire and_1_out, or_1_out;
  wire [15:0] controlled_buffer_1_out, counter_1_q;

  or or_1 (or_1_out, Jump, PCEn);
  assign controlled_buffer_1_out = Jump ? LOAD : 16'bz;  // Controlled_Buffer controlled_buffer_1
  and and_1 (and_1_out, or_1_out, Clk);
  assign BusData = PCOut ? counter_1_q : 16'bz;  // Controlled_Buffer controlled_buffer_2
  Counter #(.max('hffff), .width(16)) counter_1 (
    .load(Jump), .D(controlled_buffer_1_out), .Q(counter_1_q), .clk(and_1_out), .clr(PCClr));  // open: count, carry, up
endmodule

module MARandRAM (
  input  UpperLoad,
  input  LowerLoad,
  input  MARSel,
  input  WE,
  input  [15:0] MAR,
  input  MAREn,
  input  RO,
  input  Clk,
  input  Reset,
  input  MDREn,
  output [7:0] DATAOut
);

  wire [7:0] ram_1_dout, register_2_q, register_3_q, register_4_q;
  wire [15:0] multiplexer_1_out, register_1_q;

  Register #(.width(16)) register_1 (.D(MAR), .en(MAREn), .Q(register_1_q), .clk(Clk), .clr(Reset));
  Register register_2 (.D(MAR[7:0]), .en(UpperLoad), .Q(register_2_q), .clk(Clk), .clr(Reset));
  Register register_3 (.D(MAR[7:0]), .en(LowerLoad), .Q(register_3_q), .clk(Clk), .clr(Reset));
  Multiplexer #(.width(16)) multiplexer_1 (
    .in0(register_1_q), .in1({register_2_q, register_3_q}), .out(multiplexer_1_out), .sel(MARSel));
  Register register_4 (.D(MAR[7:0]), .en(MDREn), .Q(register_4_q), .clk(Clk), .clr(Reset));
  RAM #(.addrWidth(16), .trigger("falling")) ram_1 (
    .addr(multiplexer_1_out), .we(WE), .oe(1'b1), .clk(Clk), .din(register_4_q), .dout(ram_1_dout));
  assign DATAOut = RO ? ram_1_dout : 8'bz;  // Controlled_Buffer controlled_buffer_1

  // Notes on the sheet:
  //   INC A: 3C
  //   HLT: 76
  //   LDA: 3A
  //   DISP By: 10
  //   DISP A: 0F
  //   ADD C: 81
  //   ADD B: 80
  //   STA Addr: 32
  //   ADC B: 88
  //   MVI A, By: 3E
  //   MVI B, By: 06
  //   MVI C: 0E
endmodule

module Regs (
  input  [7:0] DataIn,
  input  Load,
  input  RegEn,
  input  Clk,
  input  Clr,
  output [7:0] CurrentData,
  output [7:0] DataOut
);

  Register register_1 (.D(DataIn), .en(Load), .Q(CurrentData), .clk(Clk), .clr(Clr));
  assign DataOut = RegEn ? CurrentData : 8'bz;  // Controlled_Buffer controlled_buffer_1
endmodule

module FlagReg (
  input  [7:0] BusALU,
  input  CarryF,
  input  Clk,
  input  Clr,
  input  FEn,
  output ZF,
  output SF,
  output CF
);

  wire [0:0] nor_1_out;

  nor nor_1 (nor_1_out[0], BusALU[0], BusALU[1], BusALU[2], BusALU[3], BusALU[4], BusALU[5], BusALU[6], BusALU[7]);
  Register #(.width(3)) register_1 (
    .D({CarryF, BusALU[7], nor_1_out[0]}), .en(FEn), .Q({CF, SF, ZF}), .clk(Clk), .clr(Clr));
endmodule

module ALU (
  input  CFIn,
  input  [7:0] A,
  input  [3:0] ALUSel,
  input  [7:0] B,
  input  ALUOut,
  output CFOut,
  output FEn,
  output [7:0] Product
);

  wire addsubcomp_1_cf, and_1_out, and_2_out, and_3_out, and_4_out, and_5_out, and_6_out, complements_1_cf,
       multiplexer_1_out, nand_1_out, or_1_out, or_2_out;
  wire [7:0] addsubcomp_1_busline, and_7_out, barrelshifter_1_numout, complements_1_busline,
       multiplexer_3_out, or_3_out, rlshifter_1_numout, xor_1_out;

  and and_1 (and_1_out, ~ALUSel[0], ~ALUSel[1], ALUSel[2], ~ALUSel[3]);  // AND_Gate
  and and_2 (and_2_out, ALUSel[0], ~ALUSel[1], ~ALUSel[2], ~ALUSel[3]);  // AND_Gate
  and and_3 (and_3_out, ALUSel[0], ALUSel[1], ~ALUSel[2], ~ALUSel[3]);  // AND_Gate
  and and_4 (and_4_out, ~ALUSel[0], ALUSel[1], ~ALUSel[2], ~ALUSel[3]);  // AND_Gate
  or or_1 (or_1_out, and_2_out, and_3_out);
  or or_2 (or_2_out, and_4_out, and_3_out);
  and and_5 (and_5_out, and_1_out, CFIn);
  and and_6 (and_6_out, ~ALUSel[0], ALUSel[1], ALUSel[2], ~ALUSel[3]);  // AND_Gate
  Complements complements_1 (.TwosComp(and_6_out), .A(A), .BusLine(complements_1_busline), .CF(complements_1_cf));
  assign and_7_out = A & B;  // AND_Gate and_7, 8 bits wide
  assign or_3_out = A | B;  // OR_Gate or_3, 8 bits wide
  AddSubComp addsubcomp_1 (
    .B(B), .Cin(and_5_out), .AddSub(or_1_out), .INC_DEC(or_2_out), .A(A), .BusLine(addsubcomp_1_busline),
    .CF(addsubcomp_1_cf));
  assign xor_1_out = A ^ B;  // XOR_Gate xor_1, 8 bits wide
  BarrelShifter barrelshifter_1 (.NumIn(A), .ShiftAmt(B[3:0]), .NumOut(barrelshifter_1_numout));
  RLShifter rlshifter_1 (.NumIn(A), .ShiftAmt(B[3:0]), .NumOut(rlshifter_1_numout));
  Multiplexer #(.select(3)) multiplexer_1 (
    .in0(addsubcomp_1_cf), .in1(addsubcomp_1_cf), .in2(addsubcomp_1_cf), .in3(addsubcomp_1_cf),
    .in4(complements_1_cf), .in5(complements_1_cf), .in6(1'b0), .in7(1'b0), .out(multiplexer_1_out),
    .sel(ALUSel[2:0]));
  nand nand_1 (nand_1_out, ~ALUSel[0], ~ALUSel[1], ALUSel[2]);  // NAND_Gate
  Multiplexer multiplexer_2 (.in0(multiplexer_1_out), .in1(1'b0), .out(CFOut), .sel(ALUSel[3]));
  assign Product = ALUOut ? multiplexer_3_out : 8'bz;  // Controlled_Buffer controlled_buffer_1
  Multiplexer #(.select(4), .width(8)) multiplexer_3 (
    .in0(addsubcomp_1_busline), .in1(addsubcomp_1_busline), .in2(addsubcomp_1_busline),
    .in3(addsubcomp_1_busline), .in4(addsubcomp_1_busline), .in5(complements_1_busline),
    .in6(complements_1_busline), .in7(xor_1_out), .in8(and_7_out), .in9(or_3_out),
    .in10(barrelshifter_1_numout), .in11(rlshifter_1_numout), .out(multiplexer_3_out), .sel(ALUSel));  // open: in12, in13, in14, in15
  and and_8 (FEn, nand_1_out, ALUOut);

  // Notes on the sheet:
  //   00: Add
  //   01: Sub
  //   02: Inc
  //   03: Dec
  //   04: ADC
endmodule

module AddSubComp (
  input  Cin,
  input  [7:0] A,
  input  AddSub,
  input  INC_DEC,
  input  [7:0] B,
  output [7:0] BusLine,
  output CF
);

  wire or_1_out;
  wire [7:0] multiplexer_1_out, xor_1_out;

  Multiplexer #(.width(8)) multiplexer_1 (.in0(B), .in1(8'h1), .out(multiplexer_1_out), .sel(INC_DEC));
  or or_1 (or_1_out, Cin, AddSub);
  Adder adder_1 (.a(A), .b(xor_1_out), .out(BusLine), .cin(or_1_out), .cout(CF));
  assign xor_1_out = {8{AddSub}} ^ multiplexer_1_out;  // XOR_Gate xor_1, 8 bits wide
endmodule

module BarrelShifter (
  input  [7:0] NumIn,
  input  [3:0] ShiftAmt,
  output [7:0] NumOut
);

  wire multiplexer_1_out, multiplexer_2_out, multiplexer_3_out, multiplexer_4_out, multiplexer_5_out,
       multiplexer_6_out, multiplexer_7_out, multiplexer_8_out, multiplexer_9_out, multiplexer_10_out,
       multiplexer_11_out, multiplexer_12_out, multiplexer_13_out, multiplexer_14_out, multiplexer_15_out,
       multiplexer_16_out, multiplexer_17_out, multiplexer_18_out, multiplexer_19_out, multiplexer_20_out,
       multiplexer_21_out, multiplexer_22_out, multiplexer_23_out, multiplexer_24_out, multiplexer_25_out,
       multiplexer_26_out, multiplexer_27_out, multiplexer_28_out, multiplexer_29_out, multiplexer_30_out,
       multiplexer_31_out, multiplexer_32_out, not_1_out;

  Multiplexer multiplexer_1 (.in0(NumIn[0]), .in1(NumIn[7]), .out(multiplexer_1_out), .sel(not_1_out));
  Multiplexer multiplexer_2 (.in0(NumIn[1]), .in1(NumIn[6]), .out(multiplexer_2_out), .sel(not_1_out));
  Multiplexer multiplexer_3 (.in0(NumIn[2]), .in1(NumIn[5]), .out(multiplexer_3_out), .sel(not_1_out));
  Multiplexer multiplexer_4 (.in0(NumIn[3]), .in1(NumIn[4]), .out(multiplexer_4_out), .sel(not_1_out));
  Multiplexer multiplexer_5 (.in0(NumIn[4]), .in1(NumIn[3]), .out(multiplexer_5_out), .sel(not_1_out));
  Multiplexer multiplexer_6 (.in0(NumIn[5]), .in1(NumIn[2]), .out(multiplexer_6_out), .sel(not_1_out));
  Multiplexer multiplexer_7 (.in0(NumIn[6]), .in1(NumIn[1]), .out(multiplexer_7_out), .sel(not_1_out));
  Multiplexer multiplexer_8 (.in0(NumIn[7]), .in1(NumIn[0]), .out(multiplexer_8_out), .sel(not_1_out));
  Multiplexer multiplexer_9 (
    .in0(multiplexer_8_out), .in1(multiplexer_7_out), .out(multiplexer_9_out), .sel(ShiftAmt[0]));
  Multiplexer multiplexer_10 (
    .in0(multiplexer_7_out), .in1(multiplexer_6_out), .out(multiplexer_10_out), .sel(ShiftAmt[0]));
  Multiplexer multiplexer_11 (
    .in0(multiplexer_6_out), .in1(multiplexer_5_out), .out(multiplexer_11_out), .sel(ShiftAmt[0]));
  Multiplexer multiplexer_12 (
    .in0(multiplexer_5_out), .in1(multiplexer_4_out), .out(multiplexer_12_out), .sel(ShiftAmt[0]));
  Multiplexer multiplexer_13 (
    .in0(multiplexer_4_out), .in1(multiplexer_3_out), .out(multiplexer_13_out), .sel(ShiftAmt[0]));
  Multiplexer multiplexer_14 (
    .in0(multiplexer_3_out), .in1(multiplexer_2_out), .out(multiplexer_14_out), .sel(ShiftAmt[0]));
  Multiplexer multiplexer_15 (
    .in0(multiplexer_2_out), .in1(multiplexer_1_out), .out(multiplexer_15_out), .sel(ShiftAmt[0]));
  Multiplexer multiplexer_16 (
    .in0(multiplexer_1_out), .in1(multiplexer_8_out), .out(multiplexer_16_out), .sel(ShiftAmt[0]));
  not not_1 (not_1_out, ShiftAmt[3]);
  Multiplexer multiplexer_17 (
    .in0(multiplexer_9_out), .in1(multiplexer_11_out), .out(multiplexer_17_out), .sel(ShiftAmt[1]));
  Multiplexer multiplexer_18 (
    .in0(multiplexer_10_out), .in1(multiplexer_12_out), .out(multiplexer_18_out), .sel(ShiftAmt[1]));
  Multiplexer multiplexer_19 (
    .in0(multiplexer_11_out), .in1(multiplexer_13_out), .out(multiplexer_19_out), .sel(ShiftAmt[1]));
  Multiplexer multiplexer_20 (
    .in0(multiplexer_12_out), .in1(multiplexer_14_out), .out(multiplexer_20_out), .sel(ShiftAmt[1]));
  Multiplexer multiplexer_21 (
    .in0(multiplexer_13_out), .in1(multiplexer_15_out), .out(multiplexer_21_out), .sel(ShiftAmt[1]));
  Multiplexer multiplexer_22 (
    .in0(multiplexer_14_out), .in1(multiplexer_16_out), .out(multiplexer_22_out), .sel(ShiftAmt[1]));
  Multiplexer multiplexer_23 (
    .in0(multiplexer_15_out), .in1(multiplexer_9_out), .out(multiplexer_23_out), .sel(ShiftAmt[1]));
  Multiplexer multiplexer_24 (
    .in0(multiplexer_16_out), .in1(multiplexer_10_out), .out(multiplexer_24_out), .sel(ShiftAmt[1]));
  Multiplexer multiplexer_25 (
    .in0(multiplexer_17_out), .in1(multiplexer_21_out), .out(multiplexer_25_out), .sel(ShiftAmt[2]));
  Multiplexer multiplexer_26 (
    .in0(multiplexer_18_out), .in1(multiplexer_22_out), .out(multiplexer_26_out), .sel(ShiftAmt[2]));
  Multiplexer multiplexer_27 (
    .in0(multiplexer_19_out), .in1(multiplexer_23_out), .out(multiplexer_27_out), .sel(ShiftAmt[2]));
  Multiplexer multiplexer_28 (
    .in0(multiplexer_20_out), .in1(multiplexer_24_out), .out(multiplexer_28_out), .sel(ShiftAmt[2]));
  Multiplexer multiplexer_29 (
    .in0(multiplexer_21_out), .in1(multiplexer_17_out), .out(multiplexer_29_out), .sel(ShiftAmt[2]));
  Multiplexer multiplexer_30 (
    .in0(multiplexer_22_out), .in1(multiplexer_18_out), .out(multiplexer_30_out), .sel(ShiftAmt[2]));
  Multiplexer multiplexer_31 (
    .in0(multiplexer_23_out), .in1(multiplexer_19_out), .out(multiplexer_31_out), .sel(ShiftAmt[2]));
  Multiplexer multiplexer_32 (
    .in0(multiplexer_24_out), .in1(multiplexer_20_out), .out(multiplexer_32_out), .sel(ShiftAmt[2]));
  Multiplexer multiplexer_33 (.in0(multiplexer_32_out), .in1(multiplexer_25_out), .out(NumOut[0]), .sel(not_1_out));
  Multiplexer multiplexer_34 (.in0(multiplexer_31_out), .in1(multiplexer_26_out), .out(NumOut[1]), .sel(not_1_out));
  Multiplexer multiplexer_35 (.in0(multiplexer_30_out), .in1(multiplexer_27_out), .out(NumOut[2]), .sel(not_1_out));
  Multiplexer multiplexer_36 (.in0(multiplexer_29_out), .in1(multiplexer_28_out), .out(NumOut[3]), .sel(not_1_out));
  Multiplexer multiplexer_37 (.in0(multiplexer_28_out), .in1(multiplexer_29_out), .out(NumOut[4]), .sel(not_1_out));
  Multiplexer multiplexer_38 (.in0(multiplexer_27_out), .in1(multiplexer_30_out), .out(NumOut[5]), .sel(not_1_out));
  Multiplexer multiplexer_39 (.in0(multiplexer_26_out), .in1(multiplexer_31_out), .out(NumOut[6]), .sel(not_1_out));
  Multiplexer multiplexer_40 (.in0(multiplexer_25_out), .in1(multiplexer_32_out), .out(NumOut[7]), .sel(not_1_out));
endmodule

module RLShifter (
  input  [7:0] NumIn,
  input  [3:0] ShiftAmt,
  output [7:0] NumOut
);

  wire multiplexer_1_out, multiplexer_2_out, multiplexer_3_out, multiplexer_4_out, multiplexer_5_out,
       multiplexer_6_out, multiplexer_7_out, multiplexer_8_out, multiplexer_9_out, multiplexer_10_out,
       multiplexer_11_out, multiplexer_12_out, multiplexer_13_out, multiplexer_14_out, multiplexer_15_out,
       multiplexer_16_out, multiplexer_17_out, multiplexer_18_out, multiplexer_19_out, multiplexer_20_out,
       multiplexer_21_out, multiplexer_22_out, multiplexer_23_out, multiplexer_24_out, multiplexer_25_out,
       multiplexer_26_out, multiplexer_27_out, multiplexer_28_out, multiplexer_29_out, multiplexer_30_out,
       multiplexer_31_out, multiplexer_32_out;

  Multiplexer multiplexer_1 (.in0(NumIn[0]), .in1(NumIn[7]), .out(multiplexer_1_out), .sel(ShiftAmt[3]));
  Multiplexer multiplexer_2 (.in0(NumIn[1]), .in1(NumIn[6]), .out(multiplexer_2_out), .sel(ShiftAmt[3]));
  Multiplexer multiplexer_3 (.in0(NumIn[2]), .in1(NumIn[5]), .out(multiplexer_3_out), .sel(ShiftAmt[3]));
  Multiplexer multiplexer_4 (.in0(NumIn[3]), .in1(NumIn[4]), .out(multiplexer_4_out), .sel(ShiftAmt[3]));
  Multiplexer multiplexer_5 (.in0(NumIn[4]), .in1(NumIn[3]), .out(multiplexer_5_out), .sel(ShiftAmt[3]));
  Multiplexer multiplexer_6 (.in0(NumIn[5]), .in1(NumIn[2]), .out(multiplexer_6_out), .sel(ShiftAmt[3]));
  Multiplexer multiplexer_7 (.in0(NumIn[6]), .in1(NumIn[1]), .out(multiplexer_7_out), .sel(ShiftAmt[3]));
  Multiplexer multiplexer_8 (.in0(NumIn[7]), .in1(NumIn[0]), .out(multiplexer_8_out), .sel(ShiftAmt[3]));
  Multiplexer multiplexer_9 (
    .in0(multiplexer_1_out), .in1(multiplexer_2_out), .out(multiplexer_9_out), .sel(ShiftAmt[0]));
  Multiplexer multiplexer_10 (
    .in0(multiplexer_2_out), .in1(multiplexer_3_out), .out(multiplexer_10_out), .sel(ShiftAmt[0]));
  Multiplexer multiplexer_11 (
    .in0(multiplexer_3_out), .in1(multiplexer_4_out), .out(multiplexer_11_out), .sel(ShiftAmt[0]));
  Multiplexer multiplexer_12 (
    .in0(multiplexer_4_out), .in1(multiplexer_5_out), .out(multiplexer_12_out), .sel(ShiftAmt[0]));
  Multiplexer multiplexer_13 (
    .in0(multiplexer_5_out), .in1(multiplexer_6_out), .out(multiplexer_13_out), .sel(ShiftAmt[0]));
  Multiplexer multiplexer_14 (
    .in0(multiplexer_6_out), .in1(multiplexer_7_out), .out(multiplexer_14_out), .sel(ShiftAmt[0]));
  Multiplexer multiplexer_15 (
    .in0(multiplexer_7_out), .in1(multiplexer_8_out), .out(multiplexer_15_out), .sel(ShiftAmt[0]));
  Multiplexer multiplexer_16 (.in0(multiplexer_8_out), .in1(1'b0), .out(multiplexer_16_out), .sel(ShiftAmt[0]));
  Multiplexer multiplexer_17 (
    .in0(multiplexer_9_out), .in1(multiplexer_11_out), .out(multiplexer_17_out), .sel(ShiftAmt[1]));
  Multiplexer multiplexer_18 (
    .in0(multiplexer_10_out), .in1(multiplexer_12_out), .out(multiplexer_18_out), .sel(ShiftAmt[1]));
  Multiplexer multiplexer_19 (
    .in0(multiplexer_11_out), .in1(multiplexer_13_out), .out(multiplexer_19_out), .sel(ShiftAmt[1]));
  Multiplexer multiplexer_20 (
    .in0(multiplexer_12_out), .in1(multiplexer_14_out), .out(multiplexer_20_out), .sel(ShiftAmt[1]));
  Multiplexer multiplexer_21 (
    .in0(multiplexer_13_out), .in1(multiplexer_15_out), .out(multiplexer_21_out), .sel(ShiftAmt[1]));
  Multiplexer multiplexer_22 (
    .in0(multiplexer_14_out), .in1(multiplexer_16_out), .out(multiplexer_22_out), .sel(ShiftAmt[1]));
  Multiplexer multiplexer_23 (.in0(multiplexer_15_out), .in1(1'b0), .out(multiplexer_23_out), .sel(ShiftAmt[1]));
  Multiplexer multiplexer_24 (.in0(multiplexer_16_out), .in1(1'b0), .out(multiplexer_24_out), .sel(ShiftAmt[1]));
  Multiplexer multiplexer_25 (
    .in0(multiplexer_17_out), .in1(multiplexer_21_out), .out(multiplexer_25_out), .sel(ShiftAmt[2]));
  Multiplexer multiplexer_26 (
    .in0(multiplexer_18_out), .in1(multiplexer_22_out), .out(multiplexer_26_out), .sel(ShiftAmt[2]));
  Multiplexer multiplexer_27 (
    .in0(multiplexer_19_out), .in1(multiplexer_23_out), .out(multiplexer_27_out), .sel(ShiftAmt[2]));
  Multiplexer multiplexer_28 (
    .in0(multiplexer_20_out), .in1(multiplexer_24_out), .out(multiplexer_28_out), .sel(ShiftAmt[2]));
  Multiplexer multiplexer_29 (.in0(multiplexer_21_out), .in1(1'b0), .out(multiplexer_29_out), .sel(ShiftAmt[2]));
  Multiplexer multiplexer_30 (.in0(multiplexer_22_out), .in1(1'b0), .out(multiplexer_30_out), .sel(ShiftAmt[2]));
  Multiplexer multiplexer_31 (.in0(multiplexer_23_out), .in1(1'b0), .out(multiplexer_31_out), .sel(ShiftAmt[2]));
  Multiplexer multiplexer_32 (.in0(multiplexer_24_out), .in1(1'b0), .out(multiplexer_32_out), .sel(ShiftAmt[2]));
  Multiplexer multiplexer_33 (.in0(multiplexer_25_out), .in1(multiplexer_32_out), .out(NumOut[0]), .sel(ShiftAmt[3]));
  Multiplexer multiplexer_34 (.in0(multiplexer_26_out), .in1(multiplexer_31_out), .out(NumOut[1]), .sel(ShiftAmt[3]));
  Multiplexer multiplexer_35 (.in0(multiplexer_27_out), .in1(multiplexer_30_out), .out(NumOut[2]), .sel(ShiftAmt[3]));
  Multiplexer multiplexer_36 (.in0(multiplexer_28_out), .in1(multiplexer_29_out), .out(NumOut[3]), .sel(ShiftAmt[3]));
  Multiplexer multiplexer_37 (.in0(multiplexer_29_out), .in1(multiplexer_28_out), .out(NumOut[4]), .sel(ShiftAmt[3]));
  Multiplexer multiplexer_38 (.in0(multiplexer_30_out), .in1(multiplexer_27_out), .out(NumOut[5]), .sel(ShiftAmt[3]));
  Multiplexer multiplexer_39 (.in0(multiplexer_31_out), .in1(multiplexer_26_out), .out(NumOut[6]), .sel(ShiftAmt[3]));
  Multiplexer multiplexer_40 (.in0(multiplexer_32_out), .in1(multiplexer_25_out), .out(NumOut[7]), .sel(ShiftAmt[3]));

  // Notes on the sheet:
  //   Bit 4 R L Select
endmodule

module Complements (
  input  TwosComp,
  input  [7:0] A,
  output [7:0] BusLine,
  output CF
);

  wire [7:0] xor_1_out;

  Adder adder_1 (.a({8{1'b0}}), .b(xor_1_out), .out(BusLine), .cin(TwosComp), .cout(CF));
  assign xor_1_out = {8{TwosComp}} ^ A;  // XOR_Gate xor_1, 8 bits wide
endmodule

module Display (
  input  UpperLoad,
  input  [7:0] BusLine,
  input  LowerLoad,
  input  Clk,
  input  Reset,
  input  DisEn,
  output [7:0] Ones,
  output [7:0] Tens,
  output [7:0] Hundreds,
  output [7:0] Thousands,
  output [7:0] TenThousands
);

  wire [7:0] register_1_q, register_2_q;
  wire [39:0] UnsignedROM_data;

  Register register_1 (.D(BusLine), .en(UpperLoad), .Q(register_1_q), .clk(Clk), .clr(Reset));
  Register register_2 (.D(BusLine), .en(LowerLoad), .Q(register_2_q), .clk(Clk), .clr(Reset));
  ROM #(.addrWidth(16), .dataWidth(40)) UnsignedROM (.addr({register_1_q, register_2_q}), .data(UnsignedROM_data));
  Register #(.width(40)) register_3 (
    .D(UnsignedROM_data), .en(DisEn), .Q({TenThousands, Thousands, Hundreds, Tens, Ones}), .clk(Clk),
    .clr(Reset));

  // Notes on the sheet:
  //   contents of UnsignedROM (hex, n*v repeats v):
  //   3f3f3f3f3f 3f3f3f3f06 3f3f3f3f5b 3f3f3f3f4f 3f3f3f3f66 3f3f3f3f6d 3f3f3f3f7c 3f3f3f3f07 3f3f3f3f7f
  //   3f3f3f3f67 3f3f3f063f 3f3f3f0606 3f3f3f065b 3f3f3f064f 3f3f3f0666 3f3f3f066d 3f3f3f067c 3f3f3f0607
  //   3f3f3f067f 3f3f3f0667 3f3f3f5b3f 3f3f3f5b06 3f3f3f5b5b 3f3f3f5b4f 3f3f3f5b66 3f3f3f5b6d 3f3f3f5b7c
  //   3f3f3f5b07 3f3f3f5b7f 3f3f3f5b67 3f3f3f4f3f 3f3f3f4f06 3f3f3f4f5b 3f3f3f4f4f 3f3f3f4f66 3f3f3f4f6d
  //   3f3f3f4f7c 3f3f3f4f07 3f3f3f4f7f 3f3f3f4f67 3f3f3f663f 3f3f3f6606 3f3f3f665b 3f3f3f664f 3f3f3f6666
  //   3f3f3f666d 3f3f3f667c 3f3f3f6607 3f3f3f667f 3f3f3f6667 3f3f3f6d3f 3f3f3f6d06 3f3f3f6d5b 3f3f3f6d4f
  //   3f3f3f6d66 3f3f3f6d6d 3f3f3f6d7c 3f3f3f6d07 3f3f3f6d7f 3f3f3f6d67 3f3f3f7c3f 3f3f3f7c06 3f3f3f7c5b
  //   3f3f3f7c4f 3f3f3f7c66 3f3f3f7c6d 3f3f3f7c7c 3f3f3f7c07 3f3f3f7c7f 3f3f3f7c67 3f3f3f073f 3f3f3f0706
  //   3f3f3f075b 3f3f3f074f 3f3f3f0766 3f3f3f076d 3f3f3f077c 3f3f3f0707 3f3f3f077f 3f3f3f0767 3f3f3f7f3f
  //   3f3f3f7f06 3f3f3f7f5b 3f3f3f7f4f 3f3f3f7f66 3f3f3f7f6d 3f3f3f7f7c 3f3f3f7f07 3f3f3f7f7f 3f3f3f7f67
  //   3f3f3f673f 3f3f3f6706 3f3f3f675b 3f3f3f674f 3f3f3f6766 3f3f3f676d 3f3f3f677c 3f3f3f6707 3f3f3f677f
  //   3f3f3f6767 3f3f063f3f 3f3f063f06 3f3f063f5b 3f3f063f4f 3f3f063f66 3f3f063f6d 3f3f063f7c 3f3f063f07
  //   3f3f063f7f 3f3f063f67 3f3f06063f 3f3f060606 3f3f06065b 3f3f06064f 3f3f060666 3f3f06066d 3f3f06067c
  //   3f3f060607 3f3f06067f 3f3f060667 3f3f065b3f 3f3f065b06 3f3f065b5b 3f3f065b4f 3f3f065b66 3f3f065b6d
  //   3f3f065b7c 3f3f065b07 3f3f065b7f 3f3f065b67 3f3f064f3f 3f3f064f06 3f3f064f5b 3f3f064f4f 3f3f064f66
  //   3f3f064f6d 3f3f064f7c 3f3f064f07 3f3f064f7f 3f3f064f67 3f3f06663f 3f3f066606 3f3f06665b 3f3f06664f
  //   3f3f066666 3f3f06666d 3f3f06667c 3f3f066607 3f3f06667f 3f3f066667 3f3f066d3f 3f3f066d06 3f3f066d5b
  //   3f3f066d4f 3f3f066d66 3f3f066d6d 3f3f066d7c 3f3f066d07 3f3f066d7f 3f3f066d67 3f3f067c3f 3f3f067c06
  //   3f3f067c5b 3f3f067c4f 3f3f067c66 3f3f067c6d 3f3f067c7c 3f3f067c07 3f3f067c7f 3f3f067c67 3f3f06073f
  //   3f3f060706 3f3f06075b 3f3f06074f 3f3f060766 3f3f06076d 3f3f06077c 3f3f060707 3f3f06077f 3f3f060767
  //   3f3f067f3f 3f3f067f06 3f3f067f5b 3f3f067f4f 3f3f067f66 3f3f067f6d 3f3f067f7c 3f3f067f07 3f3f067f7f
  //   3f3f067f67 3f3f06673f 3f3f066706 3f3f06675b 3f3f06674f 3f3f066766 3f3f06676d 3f3f06677c 3f3f066707
  //   3f3f06677f 3f3f066767 3f3f5b3f3f 3f3f5b3f06 3f3f5b3f5b 3f3f5b3f4f 3f3f5b3f66 3f3f5b3f6d 3f3f5b3f7c
  //   3f3f5b3f07 3f3f5b3f7f 3f3f5b3f67 3f3f5b063f 3f3f5b0606 3f3f5b065b 3f3f5b064f 3f3f5b0666 3f3f5b066d
  //   3f3f5b067c 3f3f5b0607 3f3f5b067f 3f3f5b0667 3f3f5b5b3f 3f3f5b5b06 3f3f5b5b5b 3f3f5b5b4f 3f3f5b5b66
  //   3f3f5b5b6d 3f3f5b5b7c 3f3f5b5b07 3f3f5b5b7f 3f3f5b5b67 3f3f5b4f3f 3f3f5b4f06 3f3f5b4f5b 3f3f5b4f4f
  //   3f3f5b4f66 3f3f5b4f6d 3f3f5b4f7c 3f3f5b4f07 3f3f5b4f7f 3f3f5b4f67 3f3f5b663f 3f3f5b6606 3f3f5b665b
  //   3f3f5b664f 3f3f5b6666 3f3f5b666d 3f3f5b667c 3f3f5b6607 3f3f5b667f 3f3f5b6667 3f3f5b6d3f 3f3f5b6d06
  //   3f3f5b6d5b 3f3f5b6d4f 3f3f5b6d66 3f3f5b6d6d 3f3f5b6d7c 3f3f5b6d07 3f3f5b6d7f 3f3f5b6d67 3f3f5b7c3f
  //   3f3f5b7c06 3f3f5b7c5b 3f3f5b7c4f 3f3f5b7c66 3f3f5b7c6d 3f3f5b7c7c 3f3f5b7c07 3f3f5b7c7f 3f3f5b7c67
  //   3f3f5b073f 3f3f5b0706 3f3f5b075b 3f3f5b074f 3f3f5b0766 3f3f5b076d 3f3f5b077c 3f3f5b0707 3f3f5b077f
  //   3f3f5b0767 3f3f5b7f3f 3f3f5b7f06 3f3f5b7f5b 3f3f5b7f4f 3f3f5b7f66 3f3f5b7f6d 3f3f5b7f7c 3f3f5b7f07
  //   3f3f5b7f7f 3f3f5b7f67 3f3f5b673f 3f3f5b6706 3f3f5b675b 3f3f5b674f 3f3f5b6766 3f3f5b676d 3f3f5b677c
  //   3f3f5b6707 3f3f5b677f 3f3f5b6767 3f3f4f3f3f 3f3f4f3f06 3f3f4f3f5b 3f3f4f3f4f 3f3f4f3f66 3f3f4f3f6d
  //   3f3f4f3f7c 3f3f4f3f07 3f3f4f3f7f 3f3f4f3f67 3f3f4f063f 3f3f4f0606 3f3f4f065b 3f3f4f064f 3f3f4f0666
  //   3f3f4f066d 3f3f4f067c 3f3f4f0607 3f3f4f067f 3f3f4f0667 3f3f4f5b3f 3f3f4f5b06 3f3f4f5b5b 3f3f4f5b4f
  //   3f3f4f5b66 3f3f4f5b6d 3f3f4f5b7c 3f3f4f5b07 3f3f4f5b7f 3f3f4f5b67 3f3f4f4f3f 3f3f4f4f06 3f3f4f4f5b
  //   3f3f4f4f4f 3f3f4f4f66 3f3f4f4f6d 3f3f4f4f7c 3f3f4f4f07 3f3f4f4f7f 3f3f4f4f67 3f3f4f663f 3f3f4f6606
  //   3f3f4f665b 3f3f4f664f 3f3f4f6666 3f3f4f666d 3f3f4f667c 3f3f4f6607 3f3f4f667f 3f3f4f6667 3f3f4f6d3f
  //   3f3f4f6d06 3f3f4f6d5b 3f3f4f6d4f 3f3f4f6d66 3f3f4f6d6d 3f3f4f6d7c 3f3f4f6d07 3f3f4f6d7f 3f3f4f6d67
  //   3f3f4f7c3f 3f3f4f7c06 3f3f4f7c5b 3f3f4f7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
endmodule

module ROMTEst (
  input  [15:0] in_1,
  input  UpperLoad,
  input  [7:0] BusLine,
  input  LowerLoad,
  input  Clk,
  input  Reset,
  input  DisEn,
  output [7:0] Ones,
  output [7:0] Tens,
  output [7:0] Hundreds,
  output [7:0] Thousands,
  output [7:0] TenThousands
);

  wire [7:0] register_1_q, register_2_q;
  wire [39:0] rom_1_data;

  Register register_1 (.D(BusLine), .en(UpperLoad), .Q(register_1_q), .clk(Clk), .clr(Reset));
  Register register_2 (.D(BusLine), .en(LowerLoad), .Q(register_2_q), .clk(Clk), .clr(Reset));
  _7_Segment_Display u_7_segment_display_1 (
    .g(TenThousands[6]), .f(TenThousands[5]), .a(TenThousands[0]), .b(TenThousands[1]), .e(TenThousands[4]),
    .d(TenThousands[3]), .c(TenThousands[2]));  // open: dp
  ROM #(.addrWidth(16), .dataWidth(40)) rom_1 (.addr(in_1), .data(rom_1_data));
  _7_Segment_Display u_7_segment_display_2 (
    .g(Thousands[6]), .f(Thousands[5]), .a(Thousands[0]), .b(Thousands[1]), .e(Thousands[4]),
    .d(Thousands[3]), .c(Thousands[2]));  // open: dp
  _7_Segment_Display u_7_segment_display_3 (
    .g(Hundreds[6]), .f(Hundreds[5]), .a(Hundreds[0]), .b(Hundreds[1]), .e(Hundreds[4]), .d(Hundreds[3]),
    .c(Hundreds[2]));  // open: dp
  _7_Segment_Display u_7_segment_display_4 (
    .g(Tens[6]), .f(Tens[5]), .a(Tens[0]), .b(Tens[1]), .e(Tens[4]), .d(Tens[3]), .c(Tens[2]));  // open: dp
  Register #(.width(40)) register_3 (
    .D(rom_1_data), .en(DisEn), .Q({TenThousands, Thousands, Hundreds, Tens, Ones}), .clk(Clk), .clr(Reset));
  _7_Segment_Display u_7_segment_display_5 (
    .g(Ones[6]), .f(Ones[5]), .a(Ones[0]), .b(Ones[1]), .e(Ones[4]), .d(Ones[3]), .c(Ones[2]));  // open: dp

  // Notes on the sheet:
  //   contents of rom_1 (hex, n*v repeats v):
  //   3f3f3f3f3f 3f3f3f3f06 3f3f3f3f5b 3f3f3f3f4f 3f3f3f3f66 3f3f3f3f6d 3f3f3f3f7c 3f3f3f3f07 3f3f3f3f7f
  //   3f3f3f3f67 3f3f3f063f 3f3f3f0606 3f3f3f065b 3f3f3f064f 3f3f3f0666 3f3f3f066d 3f3f3f067c 3f3f3f0607
  //   3f3f3f067f 3f3f3f0667 3f3f3f5b3f 3f3f3f5b06 3f3f3f5b5b 3f3f3f5b4f 3f3f3f5b66 3f3f3f5b6d 3f3f3f5b7c
  //   3f3f3f5b07 3f3f3f5b7f 3f3f3f5b67 3f3f3f4f3f 3f3f3f4f06 3f3f3f4f5b 3f3f3f4f4f 3f3f3f4f66 3f3f3f4f6d
  //   3f3f3f4f7c 3f3f3f4f07 3f3f3f4f7f 3f3f3f4f67 3f3f3f663f 3f3f3f6606 3f3f3f665b 3f3f3f664f 3f3f3f6666
  //   3f3f3f666d 3f3f3f667c 3f3f3f6607 3f3f3f667f 3f3f3f6667 3f3f3f6d3f 3f3f3f6d06 3f3f3f6d5b 3f3f3f6d4f
  //   3f3f3f6d66 3f3f3f6d6d 3f3f3f6d7c 3f3f3f6d07 3f3f3f6d7f 3f3f3f6d67 3f3f3f7c3f 3f3f3f7c06 3f3f3f7c5b
  //   3f3f3f7c4f 3f3f3f7c66 3f3f3f7c6d 3f3f3f7c7c 3f3f3f7c07 3f3f3f7c7f 3f3f3f7c67 3f3f3f073f 3f3f3f0706
  //   3f3f3f075b 3f3f3f074f 3f3f3f0766 3f3f3f076d 3f3f3f077c 3f3f3f0707 3f3f3f077f 3f3f3f0767 3f3f3f7f3f
  //   3f3f3f7f06 3f3f3f7f5b 3f3f3f7f4f 3f3f3f7f66 3f3f3f7f6d 3f3f3f7f7c 3f3f3f7f07 3f3f3f7f7f 3f3f3f7f67
  //   3f3f3f673f 3f3f3f6706 3f3f3f675b 3f3f3f674f 3f3f3f6766 3f3f3f676d 3f3f3f677c 3f3f3f6707 3f3f3f677f
  //   3f3f3f6767 3f3f063f3f 3f3f063f06 3f3f063f5b 3f3f063f4f 3f3f063f66 3f3f063f6d 3f3f063f7c 3f3f063f07
  //   3f3f063f7f 3f3f063f67 3f3f06063f 3f3f060606 3f3f06065b 3f3f06064f 3f3f060666 3f3f06066d 3f3f06067c
  //   3f3f060607 3f3f06067f 3f3f060667 3f3f065b3f 3f3f065b06 3f3f065b5b 3f3f065b4f 3f3f065b66 3f3f065b6d
  //   3f3f065b7c 3f3f065b07 3f3f065b7f 3f3f065b67 3f3f064f3f 3f3f064f06 3f3f064f5b 3f3f064f4f 3f3f064f66
  //   3f3f064f6d 3f3f064f7c 3f3f064f07 3f3f064f7f 3f3f064f67 3f3f06663f 3f3f066606 3f3f06665b 3f3f06664f
  //   3f3f066666 3f3f06666d 3f3f06667c 3f3f066607 3f3f06667f 3f3f066667 3f3f066d3f 3f3f066d06 3f3f066d5b
  //   3f3f066d4f 3f3f066d66 3f3f066d6d 3f3f066d7c 3f3f066d07 3f3f066d7f 3f3f066d67 3f3f067c3f 3f3f067c06
  //   3f3f067c5b 3f3f067c4f 3f3f067c66 3f3f067c6d 3f3f067c7c 3f3f067c07 3f3f067c7f 3f3f067c67 3f3f06073f
  //   3f3f060706 3f3f06075b 3f3f06074f 3f3f060766 3f3f06076d 3f3f06077c 3f3f060707 3f3f06077f 3f3f060767
  //   3f3f067f3f 3f3f067f06 3f3f067f5b 3f3f067f4f 3f3f067f66 3f3f067f6d 3f3f067f7c 3f3f067f07 3f3f067f7f
  //   3f3f067f67 3f3f06673f 3f3f066706 3f3f06675b 3f3f06674f 3f3f066766 3f3f06676d 3f3f06677c 3f3f066707
  //   3f3f06677f 3f3f066767 3f3f5b3f3f 3f3f5b3f06 3f3f5b3f5b 3f3f5b3f4f 3f3f5b3f66 3f3f5b3f6d 3f3f5b3f7c
  //   3f3f5b3f07 3f3f5b3f7f 3f3f5b3f67 3f3f5b063f 3f3f5b0606 3f3f5b065b 3f3f5b064f 3f3f5b0666 3f3f5b066d
  //   3f3f5b067c 3f3f5b0607 3f3f5b067f 3f3f5b0667 3f3f5b5b3f 3f3f5b5b06 3f3f5b5b5b 3f3f5b5b4f 3f3f5b5b66
  //   3f3f5b5b6d 3f3f5b5b7c 3f3f5b5b07 3f3f5b5b7f 3f3f5b5b67 3f3f5b4f3f 3f3f5b4f06 3f3f5b4f5b 3f3f5b4f4f
  //   3f3f5b4f66 3f3f5b4f6d 3f3f5b4f7c 3f3f5b4f07 3f3f5b4f7f 3f3f5b4f67 3f3f5b663f 3f3f5b6606 3f3f5b665b
  //   3f3f5b664f 3f3f5b6666 3f3f5b666d 3f3f5b667c 3f3f5b6607 3f3f5b667f 3f3f5b6667 3f3f5b6d3f 3f3f5b6d06
  //   3f3f5b6d5b 3f3f5b6d4f 3f3f5b6d66 3f3f5b6d6d 3f3f5b6d7c 3f3f5b6d07 3f3f5b6d7f 3f3f5b6d67 3f3f5b7c3f
  //   3f3f5b7c06 3f3f5b7c5b 3f3f5b7c4f 3f3f5b7c66 3f3f5b7c6d 3f3f5b7c7c 3f3f5b7c07 3f3f5b7c7f 3f3f5b7c67
  //   3f3f5b073f 3f3f5b0706 3f3f5b075b 3f3f5b074f 3f3f5b0766 3f3f5b076d 3f3f5b077c 3f3f5b0707 3f3f5b077f
  //   3f3f5b0767 3f3f5b7f3f 3f3f5b7f06 3f3f5b7f5b 3f3f5b7f4f 3f3f5b7f66 3f3f5b7f6d 3f3f5b7f7c 3f3f5b7f07
  //   3f3f5b7f7f 3f3f5b7f67 3f3f5b673f 3f3f5b6706 3f3f5b675b 3f3f5b674f 3f3f5b6766 3f3f5b676d 3f3f5b677c
  //   3f3f5b6707 3f3f5b677f 3f3f5b6767 3f3f4f3f3f 3f3f4f3f06 3f3f4f3f5b 3f3f4f3f4f 3f3f4f3f66 3f3f4f3f6d
  //   3f3f4f3f7c 3f3f4f3f07 3f3f4f3f7f 3f3f4f3f67 3f3f4f063f 3f3f4f0606 3f3f4f065b 3f3f4f064f 3f3f4f0666
  //   3f3f4f066d 3f3f4f067c 3f3f4f0607 3f3f4f067f 3f3f4f0667 3f3f4f5b3f 3f3f4f5b06 3f3f4f5b5b 3f3f4f5b4f
  //   3f3f4f5b66 3f3f4f5b6d 3f3f4f5b7c 3f3f4f5b07 3f3f4f5b7f 3f3f4f5b67 3f3f4f4f3f 3f3f4f4f06 3f3f4f4f5b
  //   3f3f4f4f4f 3f3f4f4f66 3f3f4f4f6d 3f3f4f4f7c 3f3f4f4f07 3f3f4f4f7f 3f3f4f4f67 3f3f4f663f 3f3f4f6606
  //   3f3f4f665b 3f3f4f664f 3f3f4f6666 3f3f4f666d 3f3f4f667c 3f3f4f6607 3f3f4f667f 3f3f4f6667 3f3f4f6d3f
  //   3f3f4f6d06 3f3f4f6d5b 3f3f4f6d4f 3f3f4f6d66 3f3f4f6d6d 3f3f4f6d7c 3f3f4f6d07 3f3f4f6d7f 3f3f4f6d67
  //   3f3f4f7c3f 3f3f4f7c06 3f3f4f7c5b 3f3f4f7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
endmodule

module RAMController (
  input  UpperLoad,
  input  LowerLoad,
  input  MARSel,
  input  [15:0] MAR,
  input  MAREn,
  input  Clk,
  input  Reset,
  input  MDREn,
  output [15:0] Addr,
  output [7:0] RAMWr
);

  wire [7:0] register_2_q, register_3_q;
  wire [15:0] register_1_q;

  Register #(.width(16)) register_1 (.D(MAR), .en(MAREn), .Q(register_1_q), .clk(Clk), .clr(Reset));
  Register register_2 (.D(MAR[7:0]), .en(UpperLoad), .Q(register_2_q), .clk(Clk), .clr(Reset));
  Register register_3 (.D(MAR[7:0]), .en(LowerLoad), .Q(register_3_q), .clk(Clk), .clr(Reset));
  Multiplexer #(.width(16)) multiplexer_1 (
    .in0(register_1_q), .in1({register_2_q, register_3_q}), .out(Addr), .sel(MARSel));
  Register register_4 (.D(MAR[7:0]), .en(MDREn), .Q(RAMWr), .clk(Clk), .clr(Reset));
endmodule
